# Fritzing sketch StatefulUpCounterWithOLED (saved by Fritzing 0.9.3b)
breadboards: 1

parts:
  OLED = OLED 128x64 I2C Monochrome Display
  UP = Pushbutton [package="[THT]"]
  RESET = Pushbutton [package="[THT]"]
  Power_Management_Module = USB LiPoly Charger
  Li-ion_cell = LIPO-1000mAh [package=lipo-1000]
  Arduino_Pro_Mini = Arduino Pro Mini v13

nets:
  N1: OLED.SDA, Arduino_Pro_Mini.A4
  N2: OLED.SCK, Arduino_Pro_Mini.A5
  VDD: OLED.VDD, Power_Management_Module.VBAT, Li-ion_cell.+, Arduino_Pro_Mini.VCC
  GND: OLED.GND, UP.Pin_3, UP.Pin_4, RESET.Pin_3, RESET.Pin_4, Power_Management_Module.GND, Li-ion_cell.-, Arduino_Pro_Mini.GND
  N3: UP.Pin_1, UP.Pin_2, Arduino_Pro_Mini.D9_PWM
  N4: RESET.Pin_1, RESET.Pin_2, Arduino_Pro_Mini.D2
